# Fritzing sketch Display_LCD_16x2 (saved by Fritzing 0.9.3b)
breadboards: 1

parts:
  Componente1 = Arduino Uno (Rev3)
  LCD1 = LCD screen
  U1 = POT [package=pot_mammoth]
  R1 = Resistor [tolerance=±5% resistance=220 package=THT]

nets:
  N1: Componente1.D11_PWM/MOSI, LCD1.E
  N2: Componente1.D12/MISO, LCD1.RS
  GND: Componente1.GND, LCD1.VSS, LCD1.R/W, LCD1.LED-, U1.E
  N3: Componente1.D2, LCD1.DB7
  N4: Componente1.D3_PWM, LCD1.DB6
  N5: Componente1.D4, LCD1.DB5
  N6: Componente1.D5_PWM, LCD1.DB4
  5V: Componente1.5V, LCD1.VDD, U1.S, R1.Pin_0
  N7: LCD1.V0, U1.A
  N8: LCD1.LED+, R1.Pin_1

// code stored in the sketch: DISPLAY_LCD_16X2.ino
#include <LiquidCrystal.h>//se incluye la librería
const int rs = 12, en = 11, d4 = 5, d5 = 4, d6 = 3, d7 = 2;//se nombran los pines en donde irán las patas de la pantalla
LiquidCrystal lcd(rs, en, d4, d5, d6, d7);//se heredan las caracteristicas de la librería a los pines de la pantalla 

void setup() {
lcd.begin(16, 2);//se inicia la librería denotando el numero de columnas y filas
}

void loop() {
lcd.setCursor(0, 0);//toma el cursor en la columna 0, fila 0
lcd.print("Hola mundo");//imprime un mensaje en la pantalla en la fila de arriba
lcd.setCursor(0, 1);//toma el cursor en la columna 0, fila 1
lcd.print("Hello world");//imprime un mensaje en la pantalla en la fila de abajo
}
